# Fritzing sketch sumobot (saved by Fritzing 0.9.0b)
breadboards: 1

parts:
  Part1 = Arduino Uno (Rev3)
  VCC1 = 4 x AAA Battery Mount
  J1 = Basic Servo
  J2 = Basic Servo

nets:
  N1: Part1.D9_PWM, J1.pulse
  N2: Part1.D10_PWM/SS, J2.pulse
  GND: Part1.GND, VCC1.-, J1.gnd, J2.gnd
  VCC: VCC1.+, J1.vcc, J2.vcc
